# Fritzing sketch MySimplePlotter (saved by Fritzing 0.9.3b)
breadboards: 1

parts:
  S1 = Pushbutton [package="[THT]"]
  S2 = Pushbutton [package="[THT]"]
  S3 = Pushbutton [package="[THT]"]
  R1 = Rotary Potentiometer (Small) [maximum_resistance=100kΩ package=THT]
  R2 = Rotary Potentiometer (Small) [maximum_resistance=100kΩ package=THT]
  R3 = Rotary Potentiometer (Small) [maximum_resistance=100kΩ package=THT]
  MBED1 = mbed
  R6 = Rotary Potentiometer (Small) [maximum_resistance=100kΩ package=THT]
  R7 = Rotary Potentiometer (Small) [maximum_resistance=100kΩ package=THT]
  Banggood_Display1 = Banggood Display

nets:
  N1: S1.Pin_1, S1.Pin_2, S1.Pin_3, S1.Pin_4, S2.Pin_1, S2.Pin_2, S2.Pin_3, S2.Pin_4, S3.Pin_1, S3.Pin_2, S3.Pin_3, S3.Pin_4, R1.leg2, R2.leg2, R3.leg2, MBED1.pin5, MBED1.pin6, MBED1.pin7, MBED1.VOUT, R6.leg2, R7.leg2, Banggood_Display1.VCC
  GND: R1.leg1, R2.leg1, R3.leg1, MBED1.GND, R6.leg1, R7.leg1, Banggood_Display1.GND
  N2: R1.wiper, MBED1.pin15
  N3: R2.wiper, MBED1.pin16
  N4: R3.wiper, MBED1.pin17
  N5: MBED1.pin8, Banggood_Display1.SDO
  N6: MBED1.pin9, Banggood_Display1.LED
  N7: MBED1.pin10, Banggood_Display1.SCK
  N8: MBED1.pin11, Banggood_Display1.SDI
  N9: MBED1.pin12, Banggood_Display1.DC
  N10: MBED1.pin13, Banggood_Display1.RST
  N11: MBED1.pin14, Banggood_Display1.CS
  N12: MBED1.pin18, R6.wiper
  N13: MBED1.pin19, R7.wiper
